// Logisim project project.circ as structural Verilog
module main (
  input  [3:0] in_1,
  input  [4:0] in_2,
  input  Z,
  input  [3:0] in_4
);

  wire full_adder_1_out_5, full_adder_2_out_5, full_adder_3_out_5, xor_3_out, xor_4_out;

  // XOR_Gate xor_1 has open pins: in0=Z, in4=Z, out=open
  // XOR_Gate xor_2 has open pins: in0=Z, in4=Z, out=open
  xor xor_3 (xor_3_out, Z, Z);
  xor xor_4 (xor_4_out, Z, Z);
  Full_Adder full_adder_1 (.A(Z), .C(xor_4_out), .out_4(in_2[0]), .out_5(full_adder_1_out_5));  // open: B
  Full_Adder full_adder_2 (
    .A(full_adder_1_out_5), .C(xor_3_out), .out_4(in_2[1]), .out_5(full_adder_2_out_5));  // open: B
  Full_Adder full_adder_3 (.A(full_adder_2_out_5), .out_4(in_2[2]), .out_5(full_adder_3_out_5));  // open: B, C
  Full_Adder full_adder_4 (.A(full_adder_3_out_5), .out_4(in_2[3]), .out_5(in_2[4]));  // open: B, C
  // XOR_Gate xor_5 has open pins: in0=full_adder_3_out_5, in3=in_2[4], out=open
  Decoder #(.select(4)) decoder_1 (.sel(in_2[3:0]));  // open: out0, out1, out2, out3, out4, out5, out6, out7, out8, out9, out10, out11, out12, out13, out14, out15, en
endmodule

module Full_Adder (
  input  A,
  input  B,
  input  C,
  output out_4,
  output out_5
);

  wire and_1_out, and_2_out, xor_1_out;

  xor xor_1 (xor_1_out, B, C);
  and and_1 (and_1_out, B, C);
  xor xor_2 (out_4, A, xor_1_out);
  and and_2 (and_2_out, A, xor_1_out);
  or or_1 (out_5, and_2_out, and_1_out);
endmodule
