// Logisim project assign_2_CIRCUITS.circ as structural Verilog: 4 circuits, main circuit main
module main (
  input  in_1,
  input  in_2,
  input  in_3,
  input  in_4,
  input  in_5
);

  wire _1_out, _2_out, _3_out;

  and _1 (_1_out, in_1, in_2);
  and _2 (_2_out, in_3, in_4);
  and _3 (_3_out, _1_out, _2_out);
  // AND_Gate _4 has open pins: in0=_3_out, in4=in_5, out=open
endmodule

module question_17 (
  input  A,
  input  B,
  input  C,
  input  D,
  output F
);

  wire and_1_out, and_2_out;

  and and_1 (and_1_out, A, B);
  and and_2 (and_2_out, C, D);
  and and_3 (F, and_1_out, and_2_out);
endmodule

module question_18 (
  input  in_1,
  input  in_2,
  input  in_3,
  output out_4
);

  wire _1_out, _2_out;

  and _1 (_1_out, in_1, in_2);
  buf _2 (_2_out, in_3);  // AND_Gate
  and _3 (out_4, _1_out, _2_out);
endmodule

module Question_20 (
  input  A,
  input  B,
  input  C,
  input  D,
  output F
);

  wire or_1_out, or_2_out;

  or or_1 (or_1_out, A, B);
  or or_2 (or_2_out, C, D);
  or or_3 (F, or_1_out, or_2_out);
endmodule
