// Logisim project hw5_1.2simplified.circ as structural Verilog: 1 circuit, main circuit main
module main (
  input  B,
  input  D
);

  // OR_Gate or_1 has open pins: in0=B, in4=D, out=open
endmodule
