// Logisim project hw5_1.3simplified.circ as structural Verilog: 1 circuit, main circuit main
module main (
  input  A,
  input  B,
  input  C,
  input  B_2,
  input  D,
  input  A_2,
  input  D_2
);

  wire and_1_out, and_2_out, and_3_out;

  and and_1 (and_1_out, A, B, C);
  and and_2 (and_2_out, B_2, D);
  and and_3 (and_3_out, A_2, D_2);
  // OR_Gate or_1 has open pins: in0=and_1_out, in2=and_2_out, in4=and_3_out, out=open
endmodule
