// Logisim project hw5_2.circ as structural Verilog: 1 circuit, main circuit main
module main (
  input  A,
  input  B,
  input  C,
  input  D
);

  wire and_1_out, and_3_out, and_4_out, controlled_inverter_1_out;

  Controlled_Inverter controlled_inverter_1 (.in(A), .out(controlled_inverter_1_out));  // open: en
  and and_1 (and_1_out, controlled_inverter_1_out, A, A);
  and and_2 (and_1_out, A, A);
  and and_3 (and_3_out, A, A);
  and and_4 (and_4_out, A, A);
  assign A = A ? ~A : 1'bz;  // Controlled_Inverter controlled_inverter_2
  // OR_Gate or_1 has open pins: in0=A, in1=and_1_out, in2=and_1_out, in3=and_3_out, in4=and_4_out, out=open

  assign B = A;
  assign C = A;
  assign D = A;
endmodule
