// Logisim project hw5_3.circ as structural Verilog: 1 circuit, main circuit main
module main (
  input  A,
  input  B,
  input  C
);

  wire and_1_out, and_2_out, and_3_out, controlled_inverter_1_out, controlled_inverter_2_out,
       controlled_inverter_3_out, controlled_inverter_4_out, not_1_out;

  Controlled_Inverter controlled_inverter_1 (.in(A), .out(controlled_inverter_1_out));  // open: en
  Controlled_Inverter controlled_inverter_2 (.in(B), .out(controlled_inverter_2_out));  // open: en
  Controlled_Inverter controlled_inverter_3 (.in(A), .out(controlled_inverter_3_out));  // open: en
  and and_1 (and_1_out, controlled_inverter_1_out, controlled_inverter_2_out);
  and and_2 (and_2_out, controlled_inverter_3_out, not_1_out);
  not not_1 (not_1_out, C);
  and and_3 (and_3_out, A, controlled_inverter_4_out);
  Controlled_Inverter controlled_inverter_4 (.in(B), .out(controlled_inverter_4_out));  // open: en
  // OR_Gate or_1 has open pins: in0=and_1_out, in1=and_2_out, in3=and_3_out, out=open
endmodule
