// Logisim project hw5_4.circ as structural Verilog: 1 circuit, main circuit main
module main (
  input  B,
  input  C,
  input  D
);

  wire and_1_out, and_2_out, controlled_inverter_1_out, controlled_inverter_2_out;

  Controlled_Inverter controlled_inverter_1 (.in(B), .out(controlled_inverter_1_out));  // open: en
  Controlled_Inverter controlled_inverter_2 (.in(C), .out(controlled_inverter_2_out));  // open: en
  and and_1 (and_1_out, B, D);
  and and_2 (and_2_out, controlled_inverter_1_out, controlled_inverter_2_out);
  // OR_Gate or_1 has open pins: in0=B, in2=and_1_out, in4=and_2_out, out=open
endmodule
