// Logisim project hw_1_1.1.circ as structural Verilog: 1 circuit, main circuit main
module main (
  input  A,
  input  B,
  input  C,
  input  B_2,
  input  C_2,
  input  A_2,
  input  B_3,
  input  C_3,
  input  C_4,
  input  A_3,
  input  B_4,
  input  A_4
);

  wire and_1_out, and_2_out, and_3_out, and_4_out, and_5_out;

  and and_1 (and_1_out, A, B, C);
  and and_2 (and_2_out, B_2, C_2);
  and and_3 (and_3_out, A_2, B_3, C_3);
  and and_4 (and_4_out, C_4, A_3);
  and and_5 (and_5_out, B_4, A_4);
  // OR_Gate or_1 has open pins: in0=and_1_out, in1=and_2_out, in2=and_3_out, in3=and_4_out, in4=and_5_out, out=open
endmodule
