// Logisim project hw5_4.circ as structural Verilog: 1 circuit, main circuit main
module main (
  input  in_1,
  input  in_2,
  input  in_3,
  input  in_4
);

  wire not_1_out, not_2_out, not_3_out, not_4_out, not_5_out, or_1_out, or_2_out;

  not not_1 (not_1_out, in_2);
  or or_1 (or_1_out, not_1_out, not_2_out, not_3_out, not_4_out);
  not not_2 (not_2_out, in_4);
  not not_3 (not_3_out, in_1);
  not not_4 (not_4_out, in_3);
  or or_2 (or_2_out, or_1_out, in_4);
  not not_5 (not_5_out, in_2);
  // OR_Gate or_3 has open pins: in1=not_5_out, in4=or_2_out, out=open
endmodule
