// Logisim project hw6_2.circ as structural Verilog: 1 circuit, main circuit main
module main (
  input  A,
  input  B,
  input  C,
  input  D,
  output out_5
);

  wire nor_1_out, nor_2_out, not_1_out;

  nor nor_1 (nor_1_out, A, B);
  nor nor_2 (nor_2_out, C, D);
  not not_1 (not_1_out, nor_1_out);
  or or_1 (out_5, not_1_out, nor_2_out);
endmodule
