// Logisim project hw6_5.circ as structural Verilog: 1 circuit, main circuit main
module main (
  input  A,
  input  B,
  input  C,
  input  D,
  output out_5
);

  wire not_1_out, not_2_out, not_3_out, not_4_out, not_5_out, not_6_out, not_7_out, or_1_out, or_2_out,
       or_3_out;

  not not_1 (not_1_out, A);
  not not_2 (not_2_out, B);
  or or_1 (or_1_out, not_1_out, not_2_out, not_3_out, not_4_out);
  not not_3 (not_3_out, C);
  not not_4 (not_4_out, D);
  not not_5 (not_5_out, or_1_out);
  not not_6 (not_6_out, C);
  or or_2 (or_2_out, not_5_out, not_6_out);
  not not_7 (not_7_out, A);
  or or_3 (or_3_out, not_7_out, or_2_out);
  or or_4 (out_5, or_3_out, C);
endmodule
