// Logisim project hw7_q8.circ as structural Verilog: 1 circuit, main circuit main
module main (
  input  A,
  input  B,
  input  C,
  input  D,
  input  E,
  output out_6
);

  wire xor_1_out, xor_2_out, xor_3_out;

  xor xor_1 (xor_1_out, A, B);
  xor xor_2 (xor_2_out, C, D);
  xor xor_3 (xor_3_out, xor_2_out, E);
  xor xor_4 (out_6, xor_1_out, xor_3_out);
endmodule
