// Logisim project hw_7_q2.circ as structural Verilog: 1 circuit, main circuit main
module main (
  input  A,
  input  B,
  input  C,
  input  D
);

  wire and_1_out, nand_1_out, nand_2_out, nand_3_out, nand_4_out, nand_5_out, nand_6_out, nand_7_out,
       nand_8_out, nand_9_out, nand_10_out, nand_11_out, nand_12_out;

  nand nand_1 (nand_1_out, A, A);
  nand nand_2 (nand_2_out, B, B);
  nand nand_3 (nand_3_out, C, C);
  nand nand_4 (nand_4_out, D, D);
  nand nand_5 (nand_5_out, A, A, nand_2_out, nand_2_out, nand_3_out);
  nand nand_6 (nand_6_out, nand_1_out, D);
  nand nand_7 (nand_7_out, A, nand_2_out, nand_3_out, nand_4_out);
  nand nand_8 (nand_8_out, nand_3_out, A);
  and and_1 (and_1_out, nand_5_out, nand_5_out);
  nand nand_9 (nand_9_out, nand_6_out, nand_6_out);
  nand nand_10 (nand_10_out, nand_7_out, nand_7_out);
  nand nand_11 (nand_11_out, nand_8_out, nand_8_out);
  nand nand_12 (nand_12_out, nand_9_out, and_1_out, nand_10_out, nand_11_out);
  // NAND_Gate nand_13 has open pins: in0=nand_12_out, in4=nand_12_out, out=open
endmodule
