// Logisim project hw_7_q6basic.circ as structural Verilog: 1 circuit, main circuit main
module main (
  input  A,
  input  B,
  input  C,
  output out_4
);

  wire not_1_out, not_2_out, or_1_out, or_2_out, or_3_out;

  not not_1 (not_1_out, C);
  not not_2 (not_2_out, B);
  or or_1 (or_1_out, A, B, C);
  or or_2 (or_2_out, not_1_out, B, A);
  or or_3 (or_3_out, A, C, not_2_out);
  and and_1 (out_4, or_1_out, or_2_out, or_3_out);
endmodule
