// Logisim project hw_7_q_8.circ as structural Verilog: 1 circuit, main circuit main
module main (
  input  A,
  input  B,
  input  C,
  input  D,
  output out_5
);

  wire not_1_out;

  not not_1 (not_1_out, D);
  or or_1 (out_5, A, B, C, not_1_out);
endmodule
