// Logisim project hw_8_q3.circ as structural Verilog: 1 circuit, main circuit main
module main (
  input  X,
  input  Y,
  input  Z,
  input  E
);

  wire decoder_1_out0, decoder_1_out1, decoder_1_out4, decoder_1_out5, decoder_1_out6, decoder_1_out7,
       F_1_out, F_2_out, F_3_out;

  Decoder #(.select(3)) decoder_1 (
    .out0(decoder_1_out0), .out1(decoder_1_out1), .out4(decoder_1_out4), .out5(decoder_1_out5),
    .out6(decoder_1_out6), .out7(decoder_1_out7), .en(E));  // open: out2, out3, sel
  or F_1 (F_1_out, decoder_1_out0, decoder_1_out1, decoder_1_out7);
  or F_2 (F_2_out, decoder_1_out1, decoder_1_out5);
  or F_3 (F_3_out, decoder_1_out0, decoder_1_out6);
endmodule
