// Logisim project hw_8q_4.circ as structural Verilog: 1 circuit, main circuit main
module main (
  input  A,
  input  B,
  input  C,
  input  E
);

  wire decoder_1_out0, decoder_1_out1, decoder_1_out2, decoder_1_out3, decoder_1_out4, decoder_1_out5,
       decoder_1_out6, decoder_1_out7;

  Decoder #(.select(3)) decoder_1 (
    .out0(decoder_1_out0), .out1(decoder_1_out1), .out2(decoder_1_out2), .out3(decoder_1_out3),
    .out4(decoder_1_out4), .out5(decoder_1_out5), .out6(decoder_1_out6), .out7(decoder_1_out7), .en(E));  // open: sel
  // OR_Gate F_1 has open pins: in0=decoder_1_out0, in2=decoder_1_out4, in3=decoder_1_out3, out=open
  // OR_Gate F_2 has open pins: in0=decoder_1_out2, in1=decoder_1_out1, in4=decoder_1_out7, out=open
  // OR_Gate F_3 has open pins: in0=decoder_1_out3, in1=decoder_1_out5, in2=decoder_1_out6, in3=decoder_1_out7, out=open
endmodule
