// Logisim project hw_8q_5.circ as structural Verilog: 1 circuit, main circuit main
module main (
  input  A,
  input  B,
  input  C,
  input  in_4,
  output out_5
);

  wire decoder_1_out5, decoder_1_out7, decoder_1_out8, decoder_1_out9, decoder_1_out10, decoder_1_out13,
       decoder_1_out15;

  Decoder #(.select(4)) decoder_1 (
    .out5(decoder_1_out5), .out7(decoder_1_out7), .out8(decoder_1_out8), .out9(decoder_1_out9),
    .out10(decoder_1_out10), .out13(decoder_1_out13), .out15(decoder_1_out15));  // open: out0, out1, out2, out3, out4, out6, out11, out12, out14, sel, en
  or or_1 (out_5, decoder_1_out5, decoder_1_out7, decoder_1_out8, decoder_1_out9, decoder_1_out10, decoder_1_out13, decoder_1_out15);
endmodule
