// Logisim project hw5q2.circ as structural Verilog: 1 circuit, main circuit main
module main (
  input  D,
  input  [2:0] ABC
);

  wire not_1_out;

  not not_1 (not_1_out, D);
  Multiplexer #(.select(3)) multiplexer_1 (
    .in0(D), .in1(D), .in2(not_1_out), .in3(D), .in4(D), .in5(1'b1), .in6(1'b1), .in7(not_1_out), .sel(ABC));  // open: out, en
endmodule
