// Logisim project hw5q3.circ as structural Verilog: 1 circuit, main circuit main
module main (
  input  [2:0] ABC,
  input  in_2,
  input  in_3,
  input  in_4
);

  wire decoder_1_out5, decoder_1_out6, decoder_1_out7;

  Decoder #(.select(3)) decoder_1 (
    .out5(decoder_1_out5), .out6(decoder_1_out6), .out7(decoder_1_out7), .en(ABC[0]));  // open: out0, out1, out2, out3, out4, sel
  // AND_Gate and_1 has open pins: in0=decoder_1_out7, in3=in_2, out=open
  // AND_Gate and_2 has open pins: in0=decoder_1_out6, in3=in_3, out=open
  // AND_Gate and_3 has open pins: in0=decoder_1_out5, in3=in_4, out=open
  // Pins of 1 and 3 bits meet at ABC
endmodule
