// Logisim project hw9q1.circ as structural Verilog: 1 circuit, main circuit main
module main (
  input  D,
  input  [2:0] ABC
);

  wire not_1_out;

  not not_1 (not_1_out, D);
  Multiplexer #(.select(3)) multiplexer_1 (
    .in0(D), .in3(not_1_out), .in6(1'b1), .sel(ABC));  // open: in1, in2, in4, in5, in7, out, en
endmodule
