// Logisim project hw_9_q4.circ as structural Verilog: 1 circuit, main circuit main
module main (
  input  F0,
  input  F1,
  input  F2,
  input  F3,
  input  [1:0] in_5,
  input  F4,
  input  A,
  input  F5,
  input  F6,
  input  F7,
  input  [1:0] in_11,
  output out_12
);

  wire multiplexer_1_out, multiplexer_2_out;

  Multiplexer #(.select(2)) multiplexer_1 (
    .in0(F0), .in1(F1), .in2(F2), .in3(F3), .out(multiplexer_1_out), .sel(in_5));  // open: en
  Multiplexer #(.select(2)) multiplexer_2 (
    .in0(F4), .in1(F5), .in2(F6), .in3(F7), .out(multiplexer_2_out), .sel(in_11));  // open: en
  Multiplexer multiplexer_3 (.in0(multiplexer_1_out), .in1(multiplexer_2_out), .out(out_12), .sel(A));  // open: en
endmodule
