// Logisim project hw_9_q5.circ as structural Verilog: 1 circuit, main circuit main
module main (
  input  D,
  input  [2:0] ABC
);

  wire not_1_out;

  not not_1 (not_1_out, D);
  Multiplexer #(.select(3)) multiplexer_1 (
    .in0(not_1_out), .in1(not_1_out), .in2(D), .in3(D), .in4(D), .in5(not_1_out), .in6(not_1_out), .in7(D),
    .sel(ABC));  // open: out, en
  // also tied to VCC on the sheet: not_1_out
endmodule
