// Logisim project hw_9_q5b.circ as structural Verilog
module t_table (
  input  K,
  input  L,
  input  M,
  input  N,
  output F
);

  wire and_1_out, and_2_out, and_3_out, and_4_out, not_1_out, not_2_out, not_3_out, not_4_out, not_5_out;

  not not_1 (not_1_out, L);
  and and_1 (and_1_out, not_1_out, M, not_2_out);
  not not_2 (not_2_out, N);
  and and_2 (and_2_out, L, M, N);
  and and_3 (and_3_out, K, not_3_out, not_4_out);
  not not_3 (not_3_out, M);
  not not_4 (not_4_out, N);
  and and_4 (and_4_out, K, L, not_5_out);
  not not_5 (not_5_out, M);
  or or_1 (F, and_1_out, and_2_out, and_3_out, and_4_out);
endmodule
