// Logisim project hw_12.circ as structural Verilog: 6 circuits, main circuit shift registers
module shift_registers (
  input  clock,
  input  si,
  input  reset,
  output so,
  output out_5,
  output out_6,
  output out_7
);

  D_Flip_Flop d_ff_1 (.clk(clock), .D(si), .Q(out_5), .reset(reset));  // open: Qn, preset, en
  D_Flip_Flop d_ff_2 (.clk(clock), .D(out_5), .Q(out_6), .reset(reset));  // open: Qn, preset, en
  D_Flip_Flop d_ff_3 (.clk(clock), .D(out_6), .Q(out_7), .reset(reset));  // open: Qn, preset, en
  D_Flip_Flop d_ff_4 (.clk(clock), .D(out_7), .Q(so), .reset(reset));  // open: Qn, preset, en
endmodule

module full_adder (
  input  a,
  input  b,
  input  c,
  output out_4,
  output out_5
);

  wire and_1_out, and_2_out, xor_1_out;

  xor xor_1 (xor_1_out, a, b);
  and and_1 (and_1_out, a, b);
  xor xor_2 (out_4, c, xor_1_out);
  and and_2 (and_2_out, c, xor_1_out);
  or or_1 (out_5, and_2_out, and_1_out);
endmodule

module _12_1_1 (
  input  in_1,
  input  SI,
  input  reset_1,
  input  reset_2,
  input  reset_dff,
  output [3:0] reg_a,
  output [3:0] reg_b
);

  wire clock_1_out, d_ff_1_q, full_adder_1_out_4, full_adder_1_out_5, not_1_out, or_1_out;

  Clock clock_1 (.out(clock_1_out));
  not not_1 (not_1_out, in_1);
  or or_1 (or_1_out, not_1_out, clock_1_out);
  shift_registers shift_registers_1 (
    .clock(or_1_out), .si(full_adder_1_out_4), .reset(reset_1), .out_5(reg_a[3]), .out_6(reg_a[2]),
    .out_7(reg_a[1]), .so(reg_a[0]));
  shift_registers shift_registers_2 (
    .clock(or_1_out), .si(SI), .reset(reset_2), .out_5(reg_b[3]), .out_6(reg_b[2]), .out_7(reg_b[1]),
    .so(reg_b[0]));
  full_adder full_adder_1 (
    .a(d_ff_1_q), .b(reg_a[0]), .c(reg_b[0]), .out_4(full_adder_1_out_4), .out_5(full_adder_1_out_5));
  D_Flip_Flop d_ff_1 (.clk(or_1_out), .D(full_adder_1_out_5), .Q(d_ff_1_q), .reset(reset_dff));  // open: Qn, preset, en

  // Notes on the sheet:
  //   with shift
endmodule

module _12_2 (
  input  [3:0] a,
  input  [3:0] b,
  output out_3,
  output out_4,
  output out_5,
  output out_6
);

  wire clock_1_out, full_adder_2_out_5, full_adder_3_out_5, half_adder_1_out_4;
  wire [3:0] register_2_q;
  wire [3:1] register_1_q;

  Clock clock_1 (.out(clock_1_out));
  Register #(.width(4)) register_1 (.D(a), .Q({register_1_q, register_1_q[1]}), .clk(clock_1_out));  // open: en, clr
  Register #(.width(4)) register_2 (.D(b), .Q(register_2_q), .clk(clock_1_out));  // open: en, clr
  full_adder full_adder_1 (
    .a(full_adder_2_out_5), .b(register_1_q[3]), .c(register_2_q[3]), .out_4(out_3));  // open: out_5
  full_adder full_adder_2 (
    .a(full_adder_3_out_5), .b(register_1_q[2]), .c(register_2_q[2]), .out_4(out_4),
    .out_5(full_adder_2_out_5));
  full_adder full_adder_3 (
    .a(half_adder_1_out_4), .b(register_1_q[1]), .c(register_2_q[1]), .out_4(out_6),
    .out_5(full_adder_3_out_5));
  half_adder half_adder_1 (.a(register_1_q[1]), .b(register_2_q[0]), .out_3(out_5), .out_4(half_adder_1_out_4));
endmodule

module half_adder (
  input  a,
  input  b,
  output out_3,
  output out_4
);

  xor xor_1 (out_3, a, b);
  and and_1 (out_4, a, b);
endmodule

module _12_1_2 (
  input  reset,
  input  in_2,
  input  si,
  input  reset_2,
  input  reset_3
);

  wire clock_1_out, d_ff_1_q, full_adder_1_out_4, full_adder_1_out_5, not_1_out, or_1_out,
       shift_register_1_out, shift_register_2_out;

  not not_1 (not_1_out, in_2);
  or or_1 (or_1_out, not_1_out, clock_1_out);
  Clock clock_1 (.out(clock_1_out));
  Shift_Register #(.length(4)) shift_register_1 (
    .in(full_adder_1_out_4), .clk(or_1_out), .out(shift_register_1_out), .clr(reset));  // open: shift, load, d0, q0, d1, q1, d2, q2, d3, q3
  Shift_Register #(.length(4)) shift_register_2 (
    .in(si), .clk(or_1_out), .out(shift_register_2_out), .clr(reset_2));  // open: shift, load, d0, q0, d1, q1, d2, q2, d3, q3
  D_Flip_Flop d_ff_1 (.clk(or_1_out), .D(full_adder_1_out_5), .Q(d_ff_1_q), .reset(reset_3));  // open: Qn, preset, en
  full_adder full_adder_1 (
    .a(d_ff_1_q), .b(shift_register_1_out), .c(shift_register_2_out), .out_4(full_adder_1_out_4),
    .out_5(full_adder_1_out_5));

  // Notes on the sheet:
  //   pre-shift
endmodule
