// Logisim project hw_13.circ as structural Verilog: 3 circuits, main circuit main
module main (
  input  in_1,
  input  in_2
);

  wire clock_1_out, controlled_buffer_1_out, controlled_buffer_2_out, counter_1_carry;
  wire [6:0] counter_1_q, ram_1_data, random_1_out;

  Counter #(.width(7), .max('h7f), .ongoal("load")) counter_1 (
    .Q(counter_1_q), .carry(counter_1_carry), .clk(controlled_buffer_2_out));  // open: load, D, count, clr
  assign controlled_buffer_1_out = in_1 ? clock_1_out : 1'bz;  // Controlled_Buffer controlled_buffer_1
  Clock clock_1 (.out(clock_1_out));
  Button button_1 (.out(counter_1_carry));
  assign controlled_buffer_2_out = in_2 ? clock_1_out : 1'bz;  // Controlled_Buffer controlled_buffer_2
  Random #(.width(7)) random_1 (.clk(clock_1_out), .out(random_1_out));  // open: next, clr
  RAM #(.addrWidth(7), .dataWidth(7), .bus("separate")) ram_1 (
    .addr(counter_1_q), .din(random_1_out), .data(ram_1_data), .clk(controlled_buffer_1_out));  // open: str, sel, ld, clr
  TTY #(.rows(32)) tty_1 (.data(ram_1_data), .clk(controlled_buffer_2_out));  // open: we, clr
endmodule

module ROM (
);

  wire clock_1_out;
  wire [3:0] random_1_out, rom_1_data;
  wire [6:0] bit_extender_1_out;

  Random #(.width(4)) random_1 (.clk(clock_1_out), .out(random_1_out));  // open: next, clr
  ROM_part #(.addrWidth(4), .dataWidth(4)) rom_1 (.addr(random_1_out), .data(rom_1_data));  // open: sel
  Clock clock_1 (.out(clock_1_out));
  assign bit_extender_1_out = {{3{1'b1}}, rom_1_data};  // Bit_Extender bit_extender_1
  TTY tty_1 (.data(bit_extender_1_out), .clk(clock_1_out));  // open: we, clr

  // Notes on the sheet:
  //   contents of rom_1 (hex, n*v repeats v):
  //   0 3 0 0 0 7 5*0 a 0 b 0 c
endmodule

module Traffic_Light (
);

  wire button_1_out, clock_1_out;
  wire [2:0] counter_1_q, rom_1_data;

  Clock clock_1 (.out(clock_1_out));
  Button button_1 (.out(button_1_out));
  Counter #(.width(3), .max('h7)) counter_1 (
    .Q(counter_1_q), .clk(clock_1_out), .clr(button_1_out));  // open: load, D, count, carry
  ROM_part #(.addrWidth(3), .dataWidth(3)) rom_1 (.addr(counter_1_q), .data(rom_1_data));  // open: sel
  LED led_1 (.in(rom_1_data[0]));
  LED led_2 (.in(rom_1_data[1]));
  LED led_3 (.in(rom_1_data[2]));

  // Notes on the sheet:
  //   contents of rom_1 (hex, n*v repeats v):
  //   1 3 2 4 0 4 2 1
endmodule
