// Logisim project Lab_1.2.circ as structural Verilog
module main (
  input  B,
  output A
);

  wire and_1_out, and_2_out, not_1_out, not_2_out;

  not not_1 (not_1_out, A);
  not not_2 (not_2_out, B);
  and and_1 (and_1_out, not_1_out, B);
  and and_2 (and_2_out, A, not_2_out, not_2_out);
  // OR_Gate or_1 has open pins: in0=and_1_out, in4=and_2_out, out=open
endmodule

module _2nd_circuit (
  input  A,
  input  B,
  input  in_3,
  output out_4
);

  wire A_and_B_prime_out, not_1_out;

  not not_1 (not_1_out, B);
  and A_and_B_prime (A_and_B_prime_out, A, not_1_out);
  or or_1 (out_4, A_and_B_prime_out, in_3);
endmodule
