// Logisim project quiz_2.circ as structural Verilog: 2 circuits, main circuit 7 seg decoder
module _7_seg_decoder (
  input  in_1,
  input  in_2,
  input  in_3,
  input  in_4,
  output A,
  output B,
  output C,
  output G,
  output F,
  output E,
  output D
);

  wire decoder_1_out0, decoder_1_out1, decoder_1_out2, decoder_1_out3, decoder_1_out4, decoder_1_out5,
       decoder_1_out6, decoder_1_out7, decoder_1_out8, decoder_1_out9, decoder_1_out10, decoder_1_out11,
       decoder_1_out12, decoder_1_out13, decoder_1_out14, decoder_1_out15;

  or or_1 (G, decoder_1_out15, decoder_1_out14, decoder_1_out13, decoder_1_out11, decoder_1_out10, decoder_1_out9, decoder_1_out6, decoder_1_out5, decoder_1_out4, decoder_1_out3, decoder_1_out2, decoder_1_out8);
  Decoder #(.select(4)) decoder_1 (
    .out0(decoder_1_out0), .out1(decoder_1_out1), .out2(decoder_1_out2), .out3(decoder_1_out3),
    .out4(decoder_1_out4), .out5(decoder_1_out5), .out6(decoder_1_out6), .out7(decoder_1_out7),
    .out8(decoder_1_out8), .out9(decoder_1_out9), .out10(decoder_1_out10), .out11(decoder_1_out11),
    .out12(decoder_1_out12), .out13(decoder_1_out13), .out14(decoder_1_out14), .out15(decoder_1_out15),
    .sel({in_4, in_3, in_2, in_1}));  // open: en
  or or_2 (F, decoder_1_out14, decoder_1_out12, decoder_1_out11, decoder_1_out10, decoder_1_out9, decoder_1_out15, decoder_1_out8, decoder_1_out6, decoder_1_out5, decoder_1_out4, decoder_1_out0);
  or or_3 (A, decoder_1_out0, decoder_1_out2, decoder_1_out3, decoder_1_out5, decoder_1_out6, decoder_1_out7, decoder_1_out8, decoder_1_out9, decoder_1_out10, decoder_1_out12, decoder_1_out14, decoder_1_out15);
  or or_4 (E, decoder_1_out15, decoder_1_out14, decoder_1_out13, decoder_1_out12, decoder_1_out11, decoder_1_out10, decoder_1_out8, decoder_1_out6, decoder_1_out2, decoder_1_out0);
  or or_5 (B, decoder_1_out0, decoder_1_out1, decoder_1_out2, decoder_1_out3, decoder_1_out4, decoder_1_out7, decoder_1_out8, decoder_1_out9, decoder_1_out10, decoder_1_out13);
  or or_6 (D, decoder_1_out14, decoder_1_out13, decoder_1_out12, decoder_1_out11, decoder_1_out9, decoder_1_out8, decoder_1_out6, decoder_1_out5, decoder_1_out3, decoder_1_out2, decoder_1_out0);
  or or_7 (C, decoder_1_out0, decoder_1_out1, decoder_1_out3, decoder_1_out4, decoder_1_out5, decoder_1_out6, decoder_1_out7, decoder_1_out8, decoder_1_out9, decoder_1_out10, decoder_1_out11, decoder_1_out13);
endmodule

module Main (
);

  wire and_1_out, and_2_out, clock_1_out, j_k_ff_1_q, j_k_ff_1_qn, j_k_ff_2_q, j_k_ff_2_qn, j_k_ff_3_q,
       j_k_ff_3_qn, j_k_ff_4_q, n7_seg_decoder_1_a, n7_seg_decoder_1_b, n7_seg_decoder_1_c,
       n7_seg_decoder_1_d, n7_seg_decoder_1_e, n7_seg_decoder_1_f, n7_seg_decoder_1_g;

  and and_1 (and_1_out, j_k_ff_1_qn, j_k_ff_2_qn);
  and and_2 (and_2_out, and_1_out, j_k_ff_3_qn);
  Clock clock_1 (.out(clock_1_out));
  J_K_Flip_Flop j_k_ff_1 (
    .J(1'b1), .clk(clock_1_out), .K(1'b1), .Q(j_k_ff_1_q), .Qn(j_k_ff_1_qn));  // open: preset, en, reset
  J_K_Flip_Flop j_k_ff_2 (
    .J(j_k_ff_1_qn), .clk(clock_1_out), .K(j_k_ff_1_qn), .Q(j_k_ff_2_q), .Qn(j_k_ff_2_qn));  // open: preset, en, reset
  J_K_Flip_Flop j_k_ff_3 (
    .J(and_1_out), .clk(clock_1_out), .K(and_1_out), .Q(j_k_ff_3_q), .Qn(j_k_ff_3_qn));  // open: preset, en, reset
  J_K_Flip_Flop j_k_ff_4 (
    .J(and_2_out), .clk(clock_1_out), .K(and_2_out), .Q(j_k_ff_4_q));  // open: Qn, preset, en, reset
  _7_seg_decoder u_7_seg_decoder_1 (
    .in_1(j_k_ff_1_q), .in_2(j_k_ff_2_q), .in_3(j_k_ff_3_q), .in_4(j_k_ff_4_q), .G(n7_seg_decoder_1_g),
    .F(n7_seg_decoder_1_f), .E(n7_seg_decoder_1_e), .D(n7_seg_decoder_1_d), .A(n7_seg_decoder_1_a),
    .B(n7_seg_decoder_1_b), .C(n7_seg_decoder_1_c));
  _7_Segment_Display u_7_segment_display_1 (
    .g(n7_seg_decoder_1_g), .f(n7_seg_decoder_1_f), .a(n7_seg_decoder_1_a), .b(n7_seg_decoder_1_b),
    .e(n7_seg_decoder_1_e), .d(n7_seg_decoder_1_d), .c(n7_seg_decoder_1_c));  // open: dp
endmodule
