// Logisim project exam_2_real.circ as structural Verilog
module main (
  input  A,
  input  B,
  input  C,
  output out_4
);

  wire nor_1_out, nor_2_out, nor_3_out, nor_4_out, nor_5_out, nor_6_out, nor_7_out, nor_8_out, nor_9_out,
       nor_10_out, nor_11_out, nor_12_out;

  nor nor_1 (nor_1_out, B, B);
  nor nor_2 (nor_2_out, A, A);
  nor nor_3 (nor_3_out, nor_2_out, nor_2_out);
  nor nor_4 (nor_4_out, nor_3_out, nor_1_out);
  nor nor_5 (nor_5_out, nor_2_out, B, C);
  nor nor_6 (nor_6_out, nor_1_out, C);
  nor nor_7 (nor_7_out, nor_4_out, nor_4_out);
  nor nor_8 (nor_8_out, nor_5_out, nor_5_out);
  nor nor_9 (nor_9_out, nor_6_out, nor_6_out);
  nor nor_10 (nor_10_out, nor_7_out, nor_7_out);
  nor nor_11 (nor_11_out, nor_8_out, nor_8_out);
  nor nor_12 (nor_12_out, nor_9_out, nor_9_out);
  nor nor_13 (out_4, nor_10_out, nor_11_out, nor_12_out);
endmodule

module q8 (
  input  in_1,
  input  [1:0] in_2,
  output out_3
);

  wire and_1_out, and_2_out, and_3_out, and_4_out, decoder_1_out0, decoder_1_out1, decoder_1_out2,
       decoder_1_out3;

  Decoder #(.select(2)) decoder_1 (
    .out0(decoder_1_out0), .out1(decoder_1_out1), .out2(decoder_1_out2), .out3(decoder_1_out3), .sel(in_2),
    .en(in_1));
  buf and_1 (and_1_out, decoder_1_out0);  // AND_Gate
  buf and_2 (and_2_out, decoder_1_out1);  // AND_Gate
  buf and_3 (and_3_out, decoder_1_out2);  // AND_Gate
  buf and_4 (and_4_out, decoder_1_out3);  // AND_Gate
  or or_1 (out_3, and_1_out, and_2_out, and_3_out, and_4_out);
endmodule
