// Logisim project exam_2_review.circ as structural Verilog
module main (
  input  A,
  input  B,
  input  C,
  output out_4
);

  wire nand_1_out, nand_2_out, nand_3_out, nand_4_out, nand_5_out, nand_6_out, nand_7_out, nand_8_out,
       nand_9_out, nand_10_out, nand_11_out, nand_12_out, not_1_out, not_2_out, not_3_out, not_4_out,
       not_5_out;

  not not_1 (not_1_out, A);
  not not_2 (not_2_out, B);
  not not_3 (not_3_out, B);
  not not_4 (not_4_out, C);
  not not_5 (not_5_out, A);
  nand nand_1 (nand_1_out, not_1_out, not_2_out, C);
  nand nand_2 (nand_2_out, A, not_3_out);
  nand nand_3 (nand_3_out, not_3_out, not_4_out);
  nand nand_4 (nand_4_out, not_5_out, C);
  nand nand_5 (nand_5_out, nand_1_out, nand_1_out);
  nand nand_6 (nand_6_out, nand_2_out, nand_2_out);
  nand nand_7 (nand_7_out, nand_3_out, nand_3_out);
  nand nand_8 (nand_8_out, nand_4_out, nand_4_out);
  nand nand_9 (nand_9_out, nand_5_out, nand_5_out);
  nand nand_10 (nand_10_out, nand_6_out, nand_6_out);
  nand nand_11 (nand_11_out, nand_7_out, nand_7_out);
  nand nand_12 (nand_12_out, nand_8_out, nand_8_out);
  nand nand_13 (out_4, nand_9_out, nand_10_out, nand_10_out, nand_11_out, nand_12_out);
endmodule

module q4 (
  input  A,
  input  B,
  input  C,
  input  E,
  input  F,
  input  D,
  input  G,
  output out_8
);

  wire nand_1_out, nand_2_out, nand_3_out, nand_4_out, nand_5_out, nand_6_out, nand_7_out, nand_8_out,
       nand_9_out, nand_10_out, nand_11_out, nand_12_out, nand_13_out;

  nand nand_1 (nand_1_out, A, B);
  nand nand_2 (nand_2_out, C, D);
  nand nand_3 (nand_3_out, nand_1_out, nand_1_out);
  nand nand_4 (nand_4_out, nand_2_out, nand_2_out);
  nand nand_5 (nand_5_out, nand_3_out, nand_3_out);
  nand nand_6 (nand_6_out, nand_4_out, nand_4_out);
  nand nand_7 (nand_7_out, nand_5_out, nand_6_out);
  nand nand_8 (nand_8_out, nand_7_out, E);
  nand nand_9 (nand_9_out, F, G);
  nand nand_10 (nand_10_out, nand_8_out, nand_8_out);
  nand nand_11 (nand_11_out, nand_9_out, nand_9_out);
  nand nand_12 (nand_12_out, nand_10_out, nand_10_out);
  nand nand_13 (nand_13_out, nand_11_out, nand_11_out);
  nand nand_14 (out_8, nand_12_out, nand_13_out);
endmodule

module q6 (
  input  A,
  input  B,
  input  C,
  input  D,
  input  E,
  input  F,
  output out_7
);

  wire nor_1_out, nor_2_out, nor_3_out, nor_4_out, nor_5_out, nor_6_out, nor_7_out, nor_8_out, nor_9_out,
       nor_10_out, nor_11_out, nor_12_out, nor_13_out, nor_14_out;

  nor nor_1 (nor_1_out, A, B);
  nor nor_2 (nor_2_out, C, D);
  nor nor_3 (nor_3_out, E, F);
  nor nor_4 (nor_4_out, nor_1_out, nor_1_out);
  nor nor_5 (nor_5_out, nor_2_out, nor_2_out);
  nor nor_6 (nor_6_out, nor_2_out, nor_2_out);
  nor nor_7 (nor_7_out, nor_3_out, nor_3_out);
  nor nor_8 (nor_8_out, nor_4_out, nor_4_out);
  nor nor_9 (nor_9_out, nor_5_out, nor_5_out);
  nor nor_10 (nor_10_out, nor_6_out, nor_6_out);
  nor nor_11 (nor_11_out, nor_7_out, nor_7_out);
  nor nor_12 (nor_12_out, nor_8_out, nor_9_out);
  nor nor_13 (nor_13_out, nor_10_out, nor_11_out);
  nor nor_14 (nor_14_out, nor_12_out, nor_13_out);
  nor nor_15 (out_7, nor_14_out, nor_14_out);
endmodule
