// Logisim project my_final.circ as structural Verilog: 3 circuits, main circuit main
module main (
  input  a,
  input  b,
  input  c,
  output d
);

  wire and_1_out, and_2_out, not_1_out, not_2_out;

  not not_1 (not_1_out, c);
  not not_2 (not_2_out, a);
  and and_1 (and_1_out, a, not_1_out);
  and and_2 (and_2_out, not_2_out, c);
  or or_1 (d, and_1_out, and_2_out, b);
endmodule

module _8_nand_only (
  input  a,
  input  b,
  input  c,
  output d
);

  wire nand_1_out, nand_2_out, nand_3_out, nand_4_out, nand_5_out, nand_6_out, nand_7_out, nand_8_out,
       nand_9_out;

  nand nand_1 (nand_1_out, a, a);
  nand nand_2 (nand_2_out, c, c);
  nand nand_3 (nand_3_out, nand_1_out, c);
  nand nand_4 (nand_4_out, a, nand_2_out);
  nand nand_5 (nand_5_out, nand_3_out, nand_3_out);
  nand nand_6 (nand_6_out, nand_4_out, nand_4_out);
  nand nand_7 (nand_7_out, nand_5_out, nand_5_out);
  nand nand_8 (nand_8_out, nand_6_out, nand_6_out);
  nand nand_9 (nand_9_out, b, b);
  nand nand_10 (d, nand_7_out, nand_8_out, nand_9_out);
endmodule

module _12 (
  input  [2:0] in_1,
  output out_2
);

  wire decoder_1_out0, decoder_1_out1, decoder_1_out2, decoder_1_out3, decoder_1_out4, decoder_1_out5,
       decoder_1_out6, decoder_1_out7, even_out, odd_out;

  Decoder #(.select(3)) decoder_1 (
    .out0(decoder_1_out0), .out1(decoder_1_out1), .out2(decoder_1_out2), .out3(decoder_1_out3),
    .out4(decoder_1_out4), .out5(decoder_1_out5), .out6(decoder_1_out6), .out7(decoder_1_out7), .sel(in_1));  // open: en
  or even (even_out, decoder_1_out0, decoder_1_out2, decoder_1_out4, decoder_1_out6);
  and odd (odd_out, decoder_1_out1, decoder_1_out3, decoder_1_out5, decoder_1_out7);
  or or_1 (out_2, even_out, odd_out);
endmodule
